// Logisim project 4bit_gray_code_counter.circ as structural Verilog: 1 circuit, main circuit main
module main (
  input  in_1
);

  wire clock_1_out, j_k_ff_1_q, j_k_ff_2_q, j_k_ff_3_q, j_k_ff_4_q, xor_1_out, xor_2_out, xor_3_out;

  Clock clock_1 (.out(clock_1_out));
  J_K_Flip_Flop #(.trigger("falling")) j_k_ff_1 (
    .J(1'b1), .clk(clock_1_out), .K(1'b1), .Q(j_k_ff_1_q), .reset(in_1));  // open: Qn, preset, en
  LED led_1 (.in(j_k_ff_1_q));
  xor xor_1 (xor_1_out, j_k_ff_1_q, j_k_ff_2_q);
  LED led_2 (.in(xor_1_out));
  J_K_Flip_Flop #(.trigger("falling")) j_k_ff_2 (
    .J(1'b1), .clk(j_k_ff_1_q), .K(1'b1), .Q(j_k_ff_2_q), .reset(in_1));  // open: Qn, preset, en
  LED led_3 (.in(j_k_ff_2_q));
  xor xor_2 (xor_2_out, j_k_ff_2_q, j_k_ff_3_q);
  LED led_4 (.in(xor_2_out));
  J_K_Flip_Flop #(.trigger("falling")) j_k_ff_3 (
    .J(1'b1), .clk(j_k_ff_2_q), .K(1'b1), .Q(j_k_ff_3_q), .reset(in_1));  // open: Qn, preset, en
  LED led_5 (.in(j_k_ff_3_q));
  xor xor_3 (xor_3_out, j_k_ff_3_q, j_k_ff_4_q);
  LED led_6 (.in(xor_3_out));
  J_K_Flip_Flop #(.trigger("falling")) j_k_ff_4 (
    .J(1'b1), .clk(j_k_ff_3_q), .K(1'b1), .Q(j_k_ff_4_q), .reset(in_1));  // open: Qn, preset, en
  LED led_7 (.in(j_k_ff_4_q));
  LED led_8 (.in(j_k_ff_4_q));

  // Notes on the sheet:
  //   b0
  //   g0
  //   b1
  //   g2
  //   b2
  //   g2
  //   g3
  //   b3
endmodule
