// Logisim project memory4by4.circ as structural Verilog: 1 circuit, main circuit 4*4 memory
module _4_4_memory (
  input  in_1,
  input  in_2,
  input  in_3,
  input  in_4,
  input  RESET_ALL,
  input  Write_Enable,
  input  [1:0] in_7,
  output out_8,
  output out_9,
  output out_10,
  output out_11,
  output out_12,
  output out_13,
  output out_14,
  output out_15
);

  wire and_1_out, and_2_out, and_3_out, and_4_out, and_5_out, and_6_out, and_7_out, and_8_out, and_9_out,
       and_10_out, and_11_out, and_12_out, and_13_out, and_14_out, and_15_out, and_16_out, and_17_out,
       and_18_out, and_19_out, and_20_out, and_21_out, clock_1_out, d_ff_1_q, d_ff_2_q, d_ff_3_q, d_ff_4_q,
       d_ff_5_q, d_ff_6_q, d_ff_7_q, d_ff_8_q, d_ff_9_q, d_ff_10_q, d_ff_11_q, d_ff_12_q, d_ff_13_q,
       d_ff_14_q, d_ff_15_q, d_ff_16_q;

  Clock clock_1 (.out(clock_1_out));
  and and_1 (and_1_out, and_2_out, out_12);
  and and_2 (and_2_out, clock_1_out, Write_Enable);
  D_Flip_Flop d_ff_1 (.clk(and_1_out), .D(in_1), .Q(d_ff_1_q), .reset(RESET_ALL));  // open: Qn, preset, en
  D_Flip_Flop d_ff_2 (.clk(and_1_out), .D(in_2), .Q(d_ff_2_q), .reset(RESET_ALL));  // open: Qn, preset, en
  D_Flip_Flop d_ff_3 (.clk(and_1_out), .D(in_3), .Q(d_ff_3_q), .reset(RESET_ALL));  // open: Qn, preset, en
  D_Flip_Flop d_ff_4 (.clk(and_1_out), .D(in_4), .Q(d_ff_4_q), .reset(RESET_ALL));  // open: Qn, preset, en
  Decoder #(.select(2), .enable("false")) decoder_1 (
    .out0(out_12), .out1(out_13), .out2(out_14), .out3(out_15), .sel(in_7));
  and and_3 (and_3_out, d_ff_1_q, out_12);
  and and_4 (and_4_out, d_ff_2_q, out_12);
  and and_5 (and_5_out, out_12, d_ff_3_q);
  and and_6 (and_6_out, d_ff_4_q, out_12);
  and and_7 (and_7_out, out_13, and_2_out);
  D_Flip_Flop d_ff_5 (.clk(and_7_out), .D(in_1), .Q(d_ff_5_q), .reset(RESET_ALL));  // open: Qn, preset, en
  D_Flip_Flop d_ff_6 (.clk(and_7_out), .D(in_2), .Q(d_ff_6_q), .reset(RESET_ALL));  // open: Qn, preset, en
  D_Flip_Flop d_ff_7 (.clk(and_7_out), .D(in_3), .Q(d_ff_7_q), .reset(RESET_ALL));  // open: Qn, preset, en
  D_Flip_Flop d_ff_8 (.clk(and_7_out), .D(in_4), .Q(d_ff_8_q), .reset(RESET_ALL));  // open: Qn, preset, en
  and and_8 (and_8_out, d_ff_5_q, out_13);
  and and_9 (and_9_out, out_13, d_ff_6_q);
  and and_10 (and_10_out, out_13, d_ff_7_q);
  and and_11 (and_11_out, out_13, d_ff_8_q);
  and and_12 (and_12_out, and_2_out, out_14);
  D_Flip_Flop d_ff_9 (.clk(and_12_out), .D(in_1), .Q(d_ff_9_q), .reset(RESET_ALL));  // open: Qn, preset, en
  D_Flip_Flop d_ff_10 (.clk(and_12_out), .D(in_2), .Q(d_ff_10_q), .reset(RESET_ALL));  // open: Qn, preset, en
  D_Flip_Flop d_ff_11 (.clk(and_12_out), .D(in_3), .Q(d_ff_11_q), .reset(RESET_ALL));  // open: Qn, preset, en
  D_Flip_Flop d_ff_12 (.clk(and_12_out), .D(in_4), .Q(d_ff_12_q), .reset(RESET_ALL));  // open: Qn, preset, en
  and and_13 (and_13_out, d_ff_9_q, out_14);
  and and_14 (and_14_out, d_ff_10_q, out_14);
  and and_15 (and_15_out, d_ff_11_q, out_14);
  and and_16 (and_16_out, d_ff_12_q, out_14);
  and and_17 (and_17_out, out_15, and_2_out);
  D_Flip_Flop d_ff_13 (.clk(and_17_out), .D(in_1), .Q(d_ff_13_q), .reset(RESET_ALL));  // open: Qn, preset, en
  D_Flip_Flop d_ff_14 (.clk(and_17_out), .D(in_2), .Q(d_ff_14_q), .reset(RESET_ALL));  // open: Qn, preset, en
  D_Flip_Flop d_ff_15 (.clk(and_17_out), .D(in_3), .Q(d_ff_15_q), .reset(RESET_ALL));  // open: Qn, preset, en
  D_Flip_Flop d_ff_16 (.clk(and_17_out), .D(in_4), .Q(d_ff_16_q), .reset(RESET_ALL));  // open: Qn, preset, en
  and and_18 (and_18_out, d_ff_13_q, out_15);
  and and_19 (and_19_out, d_ff_14_q, out_15);
  and and_20 (and_20_out, d_ff_15_q, out_15);
  and and_21 (and_21_out, d_ff_16_q, out_15);
  or or_1 (out_8, and_3_out, and_8_out, and_18_out, and_13_out);
  or or_2 (out_9, and_4_out, and_9_out, and_19_out, and_14_out);
  or or_3 (out_10, and_5_out, and_10_out, and_20_out, and_15_out);
  or or_4 (out_11, and_6_out, and_11_out, and_16_out, and_21_out);

  // Notes on the sheet:
  //   IN bits
  //   address decoder
  //   OUT bits
endmodule
